// Logisim project BouncingSquare.circ as structural Verilog
module datapath (
  input  Ld_ctr,
  input  Clk,
  input  Reset,
  output [6:0] X,
  output [6:0] Y,
  output [7:0] B,
  output [7:0] G,
  output [7:0] R,
  output Reset_out,
  output WriteEnable
);

  wire and_1_out, and_2_out, and_3_out, and_4_out, and_5_out, and_6_out, comparator_1_eq, comparator_2_eq,
       Complete_out, d_ff_1_q, nor_1_out, nor_2_out, not_1_out, not_2_out, not_3_out, or_1_out, or_2_out,
       or_3_out, or_4_out, or_6_out, Row_Count_carry, t_ff_1_qn, t_ff_2_qn;
  wire [3:0] Column_Count_q, Row_Count_q;
  wire [6:0] adder_1_out, adder_2_out, adder_5_out, adder_6_out, bit_extender_1_out, bit_extender_2_out,
       Counter_X_q, Counter_Y_q, R_X_q, R_Y_q;

  or or_1 (or_1_out, Ld_ctr, Complete_out);
  Counter #(.max('h7f), .width(7)) Counter_X (
    .clr(Reset), .load(Ld_ctr), .up(t_ff_1_qn), .clk(or_1_out), .D(7'b0010100), .Q(Counter_X_q));  // open: count, carry
  Adder #(.width(7)) adder_1 (.a(7'b0001111), .b(Counter_X_q), .out(adder_1_out));  // open: cin, cout
  Register #(.width(7)) R_X (.D(Counter_X_q), .en(1'b1), .clk(Clk), .Q(R_X_q), .clr(Reset));
  Counter #(.max('hf), .width(4)) Row_Count (
    .clr(or_2_out), .clk(Clk), .carry(Row_Count_carry), .Q(Row_Count_q));  // open: load, up, count, D
  or or_2 (or_2_out, Reset, not_1_out);
  not not_1 (not_1_out, 1'b1);
  nor nor_1 (nor_1_out, Counter_X_q[0], Counter_X_q[1], Counter_X_q[2], Counter_X_q[3], Counter_X_q[4], Counter_X_q[5], Counter_X_q[6]);
  not not_2 (not_2_out, t_ff_1_qn);
  and and_1 (and_1_out, adder_1_out[0], adder_1_out[1], adder_1_out[2], adder_1_out[3], adder_1_out[4], adder_1_out[5], adder_1_out[6]);
  and and_2 (and_2_out, nor_1_out, not_2_out);
  and and_3 (and_3_out, t_ff_1_qn, and_1_out);
  T_Flip_Flop t_ff_1 (.T(1'b1), .clk(or_3_out), .Qn(t_ff_1_qn));  // open: Q, reset, preset
  or or_3 (or_3_out, and_2_out, and_3_out);
  assign bit_extender_1_out = {{3{1'b0}}, Row_Count_q};  // Bit_Extender bit_extender_1
  Adder #(.width(7)) adder_2 (.a(R_X_q), .b(7'b0001111), .out(adder_2_out));  // open: cin, cout
  Adder #(.width(7)) adder_3 (.a(R_X_q), .b(bit_extender_1_out), .out(X));  // open: cin, cout
  Comparator #(.width(7)) comparator_1 (.a(adder_2_out), .b(X), .eq(comparator_1_eq));  // open: gt, lt
  D_Flip_Flop d_ff_1 (.D(Row_Count_carry), .clk(Clk), .Q(d_ff_1_q), .reset(not_1_out));  // open: Qn, preset
  Register #(.width(7)) R_Y (.D(Counter_Y_q), .en(1'b1), .clk(Clk), .Q(R_Y_q), .clr(Reset));
  and Complete (Complete_out, comparator_1_eq, comparator_2_eq);
  Counter #(.max('hf), .width(4)) Column_Count (
    .clr(or_4_out), .clk(d_ff_1_q), .Q(Column_Count_q));  // open: load, up, count, D, carry
  or or_4 (or_4_out, Reset, not_1_out);
  or or_5 (Reset_out, Reset, Complete_out);
  assign bit_extender_2_out = {{3{1'b0}}, Column_Count_q};  // Bit_Extender bit_extender_2
  Adder #(.width(7)) adder_4 (.a(R_Y_q), .b(bit_extender_2_out), .out(Y));  // open: cin, cout
  Counter #(.max('h7f), .width(7)) Counter_Y (
    .clr(Reset), .up(t_ff_2_qn), .clk(Complete_out), .Q(Counter_Y_q));  // open: load, count, D, carry
  Adder #(.width(7)) adder_5 (.a(R_Y_q), .b(7'b0001111), .out(adder_5_out));  // open: cin, cout
  Comparator #(.width(7)) comparator_2 (.a(adder_5_out), .b(Y), .eq(comparator_2_eq));  // open: gt, lt
  Adder #(.width(7)) adder_6 (.a(7'b0001111), .b(Counter_Y_q), .out(adder_6_out));  // open: cin, cout
  nor nor_2 (nor_2_out, Counter_Y_q[0], Counter_Y_q[1], Counter_Y_q[2], Counter_Y_q[3], Counter_Y_q[4], Counter_Y_q[5], Counter_Y_q[6]);
  and and_4 (and_4_out, adder_6_out[0], adder_6_out[1], adder_6_out[2], adder_6_out[3], adder_6_out[4], adder_6_out[5], adder_6_out[6]);
  and and_5 (and_5_out, nor_2_out, not_3_out);
  not not_3 (not_3_out, t_ff_2_qn);
  and and_6 (and_6_out, t_ff_2_qn, and_4_out);
  T_Flip_Flop t_ff_2 (.T(1'b1), .clk(or_6_out), .Qn(t_ff_2_qn));  // open: Q, reset, preset
  or or_6 (or_6_out, and_5_out, and_6_out);

  assign B = 8'h80;
  assign G = 8'h80;
  assign R = {8{1'b0}};
  assign WriteEnable = 1'b1;
endmodule

module part3_next_state (
  input  [1:0] state,
  input  Reset,
  output [1:0] next_state
);

  wire [1:0] multiplexer_1_out;

  Multiplexer #(.enable("false"), .select(2), .width(2)) multiplexer_1 (
    .in0(2'b01), .in1(2'b10), .in2(2'b10), .out(multiplexer_1_out), .sel(state));  // open: in3
  Multiplexer #(.enable("false"), .width(2)) multiplexer_2 (
    .in0(multiplexer_1_out), .in1(2'b00), .out(next_state), .sel(Reset));
endmodule

module state_table (
  input  [1:0] state,
  input  Reset,
  output [1:0] next_state,
  output Reset_out,
  output Ld_ctr
);

  part3_next_state part3_next_state_1 (.state(state), .Reset(Reset), .next_state(next_state));
  Reset_state_table reset_state_table_1 (.state(state), .Reset(Reset_out));
  ld_ctr_state_table ld_ctr_state_table_1 (.state(state), .Ld_ctr(Ld_ctr));
endmodule

module FSM (
  input  Reset
);

  wire clock_1_out, datapath_1_reset_out, datapath_1_writeenable, delaycounter_1_clk_out, or_1_out,
       state_table_1_ld_ctr, state_table_1_reset_out;
  wire [1:0] register_1_q, state_table_1_next_state;
  wire [6:0] datapath_1_x, datapath_1_y;
  wire [23:0] datapath_1_b;

  Clock clock_1 (.out(clock_1_out));
  DelayCounter delaycounter_1 (.Clk(clock_1_out), .Clk_out(delaycounter_1_clk_out));
  state_table state_table_1 (
    .state(register_1_q), .Reset(Reset), .next_state(state_table_1_next_state),
    .Reset_out(state_table_1_reset_out), .Ld_ctr(state_table_1_ld_ctr));
  Register #(.width(2)) register_1 (
    .D(state_table_1_next_state), .clk(delaycounter_1_clk_out), .Q(register_1_q), .clr(Reset));  // open: en
  or or_1 (or_1_out, state_table_1_reset_out, Reset);
  datapath datapath_1 (
    .Ld_ctr(state_table_1_ld_ctr), .Clk(delaycounter_1_clk_out), .Reset(or_1_out), .X(datapath_1_x),
    .Y(datapath_1_y), .B(datapath_1_b[7:0]), .G(datapath_1_b[15:8]), .R(datapath_1_b[23:16]),
    .Reset_out(datapath_1_reset_out), .WriteEnable(datapath_1_writeenable));
  // RGB_Video #(.cursor("No Cursor")) rgb_video_1: pin names not known; wires that end beside it: datapath_1_reset_out, delaycounter_1_clk_out, datapath_1_writeenable, datapath_1_x, datapath_1_y, datapath_1_b
endmodule

module test_datapath (
  input  Ld_ctr,
  input  Reset,
  output [6:0] X,
  output [6:0] Y
);

  wire and_1_out, and_2_out, and_3_out, and_4_out, and_5_out, and_6_out, clock_1_out, comparator_1_eq,
       comparator_2_eq, Complete_out, d_ff_1_q, nor_1_out, nor_2_out, not_1_out, not_2_out, not_3_out,
       or_1_out, or_2_out, or_3_out, or_4_out, or_5_out, or_6_out, Row_Count_carry, t_ff_1_qn, t_ff_2_qn;
  wire [3:0] Column_Count_q, Row_Count_q;
  wire [6:0] adder_1_out, adder_2_out, adder_5_out, adder_6_out, bit_extender_1_out, bit_extender_2_out,
       Counter_X_q, Counter_Y_q, R_X_q, R_Y_q;

  Clock clock_1 (.out(clock_1_out));
  or or_1 (or_1_out, Ld_ctr, Complete_out);
  Counter #(.max('h7f), .width(7)) Counter_X (
    .clr(Reset), .load(Ld_ctr), .up(t_ff_1_qn), .clk(or_1_out), .D(7'b1100100), .Q(Counter_X_q));  // open: count, carry
  Adder #(.width(7)) adder_1 (.a(7'b0001111), .b(Counter_X_q), .out(adder_1_out));  // open: cin, cout
  Register #(.width(7)) R_X (.D(Counter_X_q), .en(1'b1), .clk(clock_1_out), .Q(R_X_q), .clr(Reset));
  nor nor_1 (nor_1_out, Counter_X_q[0], Counter_X_q[1], Counter_X_q[2], Counter_X_q[3], Counter_X_q[4], Counter_X_q[5], Counter_X_q[6]);
  and and_1 (and_1_out, adder_1_out[0], adder_1_out[1], adder_1_out[2], adder_1_out[3], adder_1_out[4], adder_1_out[5], adder_1_out[6]);
  Counter #(.max('hf), .width(4)) Row_Count (
    .clr(or_2_out), .clk(clock_1_out), .carry(Row_Count_carry), .Q(Row_Count_q));  // open: load, up, count, D
  or or_2 (or_2_out, Reset, not_1_out);
  not not_1 (not_1_out, 1'b1);
  not not_2 (not_2_out, t_ff_1_qn);
  and and_2 (and_2_out, nor_1_out, not_2_out);
  and and_3 (and_3_out, t_ff_1_qn, and_1_out);
  T_Flip_Flop t_ff_1 (.T(1'b1), .clk(or_3_out), .Qn(t_ff_1_qn));  // open: Q, reset, preset
  or or_3 (or_3_out, and_2_out, and_3_out);
  assign bit_extender_1_out = {{3{1'b0}}, Row_Count_q};  // Bit_Extender bit_extender_1
  Adder #(.width(7)) adder_2 (.a(R_X_q), .b(7'b0001111), .out(adder_2_out));  // open: cin, cout
  Adder #(.width(7)) adder_3 (.a(R_X_q), .b(bit_extender_1_out), .out(X));  // open: cin, cout
  Comparator #(.width(7)) comparator_1 (.a(adder_2_out), .b(X), .eq(comparator_1_eq));  // open: gt, lt
  D_Flip_Flop d_ff_1 (.D(Row_Count_carry), .clk(clock_1_out), .Q(d_ff_1_q), .reset(not_1_out));  // open: Qn, preset
  Register #(.width(7)) R_Y (.D(Counter_Y_q), .en(1'b1), .clk(clock_1_out), .Q(R_Y_q), .clr(Reset));
  and Complete (Complete_out, comparator_1_eq, comparator_2_eq);
  Counter #(.max('hf), .width(4)) Column_Count (
    .clr(or_4_out), .clk(d_ff_1_q), .Q(Column_Count_q));  // open: load, up, count, D, carry
  or or_4 (or_4_out, Reset, not_1_out);
  or or_5 (or_5_out, Reset, Complete_out);
  // RGB_Video #(.cursor("No Cursor")) rgb_video_1: pin names not known; wires that end beside it: or_5_out, clock_1_out, 1'b1, X, Y, 24'h8080
  assign bit_extender_2_out = {{3{1'b0}}, Column_Count_q};  // Bit_Extender bit_extender_2
  Adder #(.width(7)) adder_4 (.a(R_Y_q), .b(bit_extender_2_out), .out(Y));  // open: cin, cout
  Counter #(.max('h7f), .width(7)) Counter_Y (
    .clr(Reset), .up(t_ff_2_qn), .clk(Complete_out), .Q(Counter_Y_q));  // open: load, count, D, carry
  Adder #(.width(7)) adder_5 (.a(R_Y_q), .b(7'b0001111), .out(adder_5_out));  // open: cin, cout
  Comparator #(.width(7)) comparator_2 (.a(adder_5_out), .b(Y), .eq(comparator_2_eq));  // open: gt, lt
  Adder #(.width(7)) adder_6 (.a(7'b0001111), .b(Counter_Y_q), .out(adder_6_out));  // open: cin, cout
  nor nor_2 (nor_2_out, Counter_Y_q[0], Counter_Y_q[1], Counter_Y_q[2], Counter_Y_q[3], Counter_Y_q[4], Counter_Y_q[5], Counter_Y_q[6]);
  not not_3 (not_3_out, t_ff_2_qn);
  and and_4 (and_4_out, adder_6_out[0], adder_6_out[1], adder_6_out[2], adder_6_out[3], adder_6_out[4], adder_6_out[5], adder_6_out[6]);
  and and_5 (and_5_out, nor_2_out, not_3_out);
  and and_6 (and_6_out, t_ff_2_qn, and_4_out);
  T_Flip_Flop t_ff_2 (.T(1'b1), .clk(or_6_out), .Qn(t_ff_2_qn));  // open: Q, reset, preset
  or or_6 (or_6_out, and_5_out, and_6_out);
endmodule

module Reset_state_table (
  input  [1:0] state,
  output Reset
);

  nor nor_1 (Reset, state[0], state[1]);
endmodule

module ld_ctr_state_table (
  input  [1:0] state,
  output Ld_ctr
);

  wire not_1_out;

  not not_1 (not_1_out, state[1]);
  and and_1 (Ld_ctr, state[0], not_1_out);
endmodule

module DelayCounter (
  input  Clk,
  output Clk_out
);

  Counter #(.max('h1), .width(1)) counter_1 (.clk(Clk));  // open: clr, load, up, count, D, carry, Q

  assign Clk_out = Clk;
endmodule
