// Logisim project HexDecoder.circ as structural Verilog: 9 circuits, main circuit main
module main (
  input  [3:0] c3_c2_c1_c0
);

  wire hex_decoder_1_hex0, hex_decoder_1_hex1, hex_decoder_1_hex2, hex_decoder_1_hex3, hex_decoder_1_hex4,
       hex_decoder_1_hex5, hex_decoder_1_hex6;

  HEX_Decoder hex_decoder_1 (
    .c_0(c3_c2_c1_c0[0]), .c_1(c3_c2_c1_c0[1]), .c_2(c3_c2_c1_c0[2]), .c_3(c3_c2_c1_c0[3]),
    .HEX0(hex_decoder_1_hex0), .HEX1(hex_decoder_1_hex1), .HEX2(hex_decoder_1_hex2),
    .HEX3(hex_decoder_1_hex3), .HEX4(hex_decoder_1_hex4), .HEX5(hex_decoder_1_hex5), .HEX6(hex_decoder_1_hex6));
  _7_Segment_Display #(.active("false")) u_7_segment_display_1 (
    .g(hex_decoder_1_hex6), .f(hex_decoder_1_hex5), .a(hex_decoder_1_hex0), .b(hex_decoder_1_hex1),
    .e(hex_decoder_1_hex4), .d(hex_decoder_1_hex3), .c(hex_decoder_1_hex2), .dp(1'b1));
endmodule

module seg0 (
  input  c_0,
  input  c_1,
  input  c_2,
  input  c_3,
  output HEX0
);

  wire not_1_out, not_2_out, not_3_out, not_4_out, or_1_out, or_2_out, or_3_out, or_4_out, or_5_out, or_6_out;

  not not_1 (not_1_out, c_1);
  not not_2 (not_2_out, c_2);
  not not_3 (not_3_out, c_3);
  not not_4 (not_4_out, c_0);
  or or_1 (or_1_out, c_0, c_2);
  or or_2 (or_2_out, c_0, not_3_out);
  or or_3 (or_3_out, c_1, not_3_out, c_2);
  or or_4 (or_4_out, not_4_out, c_3, not_2_out);
  or or_5 (or_5_out, not_1_out, c_3);
  or or_6 (or_6_out, not_1_out, not_2_out);
  and and_1 (HEX0, or_1_out, or_2_out, or_3_out, or_4_out, or_5_out, or_6_out);
endmodule

module seg1 (
  input  c_0,
  input  c_1,
  input  c_2,
  input  c_3,
  output HEX1
);

  wire not_1_out, not_2_out, not_3_out, or_1_out, or_2_out, or_3_out, or_4_out, or_5_out, or_6_out;

  not not_1 (not_1_out, c_0);
  not not_2 (not_2_out, c_1);
  not not_3 (not_3_out, c_3);
  or or_1 (or_1_out, c_0, c_2, not_3_out);
  or or_2 (or_2_out, c_0, c_1, c_3);
  or or_3 (or_3_out, not_1_out, not_2_out, c_3);
  or or_4 (or_4_out, c_2, c_3);
  or or_5 (or_5_out, c_1, not_1_out, not_3_out);
  or or_6 (or_6_out, c_1, not_3_out, c_2);
  and and_1 (HEX1, or_1_out, or_2_out, or_3_out, or_4_out, or_5_out, or_6_out);
endmodule

module seg2 (
  input  c_0,
  input  c_1,
  input  c_2,
  input  c_3,
  output HEX2
);

  wire not_1_out, not_2_out, not_3_out, or_1_out, or_2_out, or_3_out, or_4_out, or_5_out;

  not not_1 (not_1_out, c_0);
  not not_2 (not_2_out, c_2);
  not not_3 (not_3_out, c_3);
  or or_1 (or_1_out, not_1_out, c_1);
  or or_2 (or_2_out, not_1_out, c_3);
  or or_3 (or_3_out, c_1, c_3);
  or or_4 (or_4_out, not_2_out, c_3);
  or or_5 (or_5_out, c_2, not_3_out);
  and and_1 (HEX2, or_1_out, or_2_out, or_3_out, or_4_out, or_5_out);
endmodule

module seg3 (
  input  c_0,
  input  c_1,
  input  c_2,
  input  c_3,
  output HEX3
);

  wire not_1_out, not_2_out, not_3_out, not_4_out, or_1_out, or_2_out, or_3_out, or_4_out, or_5_out, or_6_out;

  not not_1 (not_1_out, c_0);
  not not_2 (not_2_out, c_1);
  not not_3 (not_3_out, c_2);
  not not_4 (not_4_out, c_3);
  or or_1 (or_1_out, c_1, c_0, c_2);
  or or_2 (or_2_out, c_1, c_0, not_4_out);
  or or_3 (or_3_out, c_1, not_1_out, not_3_out);
  or or_4 (or_4_out, not_2_out, not_1_out, c_2);
  or or_5 (or_5_out, not_2_out, c_3, c_2);
  or or_6 (or_6_out, not_2_out, c_0, not_3_out);
  and and_1 (HEX3, or_1_out, or_2_out, or_3_out, or_4_out, or_5_out, or_6_out);
endmodule

module seg4 (
  input  c_0,
  input  c_1,
  input  c_2,
  input  c_3,
  output HEX4
);

  wire not_1_out, not_2_out, not_3_out, not_4_out, or_1_out, or_2_out, or_3_out, or_4_out, or_5_out;

  not not_1 (not_1_out, c_0);
  not not_2 (not_2_out, c_1);
  not not_3 (not_3_out, c_2);
  not not_4 (not_4_out, c_3);
  or or_1 (or_1_out, c_0, not_2_out);
  or or_2 (or_2_out, c_1, c_0, not_4_out);
  or or_3 (or_3_out, c_1, c_0, c_2);
  or or_4 (or_4_out, not_2_out, not_1_out, not_4_out);
  or or_5 (or_5_out, not_3_out, not_4_out);
  and and_1 (HEX4, or_1_out, or_2_out, or_3_out, or_4_out, or_5_out);
endmodule

module seg5 (
  input  c_0,
  input  c_1,
  input  c_2,
  input  c_3,
  output HEX5
);

  wire not_1_out, not_2_out, not_3_out, not_4_out, or_1_out, or_2_out, or_3_out, or_4_out, or_5_out;

  not not_1 (not_1_out, c_0);
  not not_2 (not_2_out, c_1);
  not not_3 (not_3_out, c_2);
  not not_4 (not_4_out, c_3);
  or or_1 (or_1_out, c_1, c_0);
  or or_2 (or_2_out, not_2_out, not_1_out, not_4_out);
  or or_3 (or_3_out, not_2_out, c_0, not_3_out);
  or or_4 (or_4_out, c_1, not_3_out, c_3);
  or or_5 (or_5_out, c_2, not_4_out);
  and and_1 (HEX5, or_1_out, or_2_out, or_3_out, or_4_out, or_5_out);
endmodule

module seg6 (
  input  c_0,
  input  c_1,
  input  c_2,
  input  c_3,
  output HEX6
);

  wire not_1_out, not_2_out, not_3_out, not_4_out, or_1_out, or_2_out, or_3_out, or_4_out, or_5_out, or_6_out;

  not not_1 (not_1_out, c_0);
  not not_2 (not_2_out, c_1);
  not not_3 (not_3_out, c_2);
  not not_4 (not_4_out, c_3);
  or or_1 (or_1_out, not_2_out, c_0);
  or or_2 (or_2_out, not_1_out, not_4_out);
  or or_3 (or_3_out, not_2_out, c_2, c_3);
  or or_4 (or_4_out, c_1, c_3, not_3_out);
  or or_5 (or_5_out, c_2, not_4_out);
  or or_6 (or_6_out, not_2_out, not_4_out);
  and and_1 (HEX6, or_1_out, or_2_out, or_3_out, or_4_out, or_5_out, or_6_out);
endmodule

module HEX_Decoder (
  input  c_0,
  input  c_1,
  input  c_2,
  input  c_3,
  output HEX0,
  output HEX1,
  output HEX2,
  output HEX3,
  output HEX4,
  output HEX5,
  output HEX6
);

  seg0 seg0_1 (.c_0(c_0), .c_1(c_1), .c_2(c_2), .c_3(c_3), .HEX0(HEX0));
  seg1 seg1_1 (.c_0(c_0), .c_1(c_1), .c_2(c_2), .c_3(c_3), .HEX1(HEX1));
  seg2 seg2_1 (.c_0(c_0), .c_1(c_1), .c_2(c_2), .c_3(c_3), .HEX2(HEX2));
  seg3 seg3_1 (.c_0(c_0), .c_1(c_1), .c_2(c_2), .c_3(c_3), .HEX3(HEX3));
  seg4 seg4_1 (.c_0(c_0), .c_1(c_1), .c_2(c_2), .c_3(c_3), .HEX4(HEX4));
  seg5 seg5_1 (.c_0(c_0), .c_1(c_1), .c_2(c_2), .c_3(c_3), .HEX5(HEX5));
  seg6 seg6_1 (.c_0(c_0), .c_1(c_1), .c_2(c_2), .c_3(c_3), .HEX6(HEX6));
endmodule
