// Logisim project MorseCodeDecoder.circ as structural Verilog: 4 circuits, main circuit main
module main (
  input  SW_0,
  input  SW_1,
  input  SW_2,
  output [13:0] out_4
);

  wire clock_1_out, KEY_0_out, KEY_1_out, ratedivider_1_counter_out, shiftregister_1_shifted_out;
  wire [13:0] lut_1_lut_out;

  Button KEY_0 (.out(KEY_0_out));
  Button KEY_1 (.out(KEY_1_out));
  Clock clock_1 (.out(clock_1_out));
  RateDivider ratedivider_1 (
    .clear(KEY_0_out), .Clk(clock_1_out), .enable(1'b1), .counter_out(ratedivider_1_counter_out));
  LUT lut_1 (.Letter({SW_2, SW_1, SW_0}), .LUT_out(lut_1_lut_out));
  ShiftRegister shiftregister_1 (
    .reset(KEY_0_out), .load(KEY_1_out), .shift(ratedivider_1_counter_out), .Clk(clock_1_out),
    .load_val(lut_1_lut_out), .shifted(out_4), .shifted_out(shiftregister_1_shifted_out));
  LED LEDR_0 (.in(shiftregister_1_shifted_out));
endmodule

module LUT (
  input  [2:0] Letter,
  output [13:0] LUT_out
);

  Multiplexer #(.enable("false"), .select(3), .width(14)) multiplexer_1 (
    .in0(14'h2a00), .in1(14'h3800), .in2(14'h2b80), .in3(14'h2ae0), .in4(14'h2ee0), .in5(14'h3ab8),
    .in6(14'h3aee), .in7(14'h3ba8), .out(LUT_out), .sel(Letter));
endmodule

module ShiftRegister (
  input  reset,
  input  load,
  input  shift,
  input  Clk,
  input  [13:0] load_val,
  output [13:0] shifted,
  output shifted_out
);

  // Shift_Register #(.length(14)) shift_register_1: pin names not known; wires that end beside it: reset, load, shift, Clk, 1'b0, load_val[0], load_val[1], load_val[2], load_val[3], load_val[4], load_val[5], load_val[6], load_val[7], load_val[8], load_val[9], load_val[10], load_val[11], shifted[0], shifted[1], shifted[2], shifted[3], shifted[4], shifted[5], shifted[6], shifted[7], shifted[8], shifted[9], shifted[10], shifted[11]

  assign shifted_out = shifted[13];
endmodule

module RateDivider (
  input  clear,
  input  Clk,
  input  enable,
  output counter_out
);

  wire not_1_out, not_2_out, not_3_out, not_4_out, not_5_out, not_6_out, or_1_out;
  wire [5:0] counter_1_q;

  not not_1 (not_1_out, enable);
  or or_1 (or_1_out, counter_out, not_1_out);
  Counter #(.max('h3f), .width(6)) counter_1 (
    .clr(clear), .load(or_1_out), .up(1'b1), .clk(Clk), .D({6{1'b0}}), .Q(counter_1_q));  // open: count, carry
  not not_2 (not_2_out, counter_1_q[0]);
  not not_3 (not_3_out, counter_1_q[1]);
  not not_4 (not_4_out, counter_1_q[3]);
  not not_5 (not_5_out, counter_1_q[4]);
  not not_6 (not_6_out, counter_1_q[5]);
  and and_1 (counter_out, not_2_out, not_3_out, counter_1_q[2], not_4_out, not_5_out, not_6_out);
endmodule
