// Logisim project RestoringDivider.circ as structural Verilog
module datapath (
  input  [3:0] Dividend_Val,
  input  ld_Div_out,
  input  [3:0] Divisor_Val,
  input  ld_divisor,
  input  Clk,
  input  ld_Div,
  input  shift_Div,
  input  Sub,
  input  ld_quotient,
  input  ld_MSB,
  input  ld_sum,
  input  ld_rem,
  input  ld_RegA,
  input  Reset,
  output [3:0] Quotient,
  output MSB,
  output [4:0] Remainder
);

  wire [2:0] not_1_out;
  wire [3:0] multiplexer_2_out;
  wire [4:0] Dividend_p12, Divisor_q, five_bit_add_sub_1_sum, multiplexer_1_out;
  wire [4:4] Register_A_q;

  Register #(.width(5)) Divisor (.D({1'b0, Divisor_Val}), .en(ld_divisor), .clk(Clk), .Q(Divisor_q), .clr(Reset));
  five_bit_add_sub five_bit_add_sub_1 (
    .Sub(Sub), .X({Register_A_q[4], Dividend_p12[4:1]}), .Y(Divisor_q), .sum(five_bit_add_sub_1_sum));
  Multiplexer #(.enable("false"), .width(5)) multiplexer_1 (
    .in0(Dividend_p12), .in1(five_bit_add_sub_1_sum), .out(multiplexer_1_out), .sel(ld_sum));
  Multiplexer #(.enable("false"), .width(4)) multiplexer_2 (
    .in0(Dividend_Val), .in1({Dividend_p12[0], not_1_out}), .out(multiplexer_2_out), .sel(ld_Div_out));
  // Shift_Register #(.length(4)) Dividend: pin names not known; wires that end beside it: Reset, ld_Div, shift_Div, Clk, 1'b0, multiplexer_2_out[0], multiplexer_2_out[1], multiplexer_2_out[2], multiplexer_2_out[3], not_1_out[1], not_1_out[2], Dividend_p12[0]
  Register #(.width(5)) Register_A (
    .D(multiplexer_1_out), .en(ld_RegA), .clk(Clk), .Q({Register_A_q[4], Dividend_p12[4:1]}), .clr(Reset));
  not not_1 (not_1_out[0], MSB);
  D_Latch d_latch_1 (.D(Register_A_q[4]), .Clk(ld_MSB), .Qa(MSB));  // open: Qb
  Register #(.width(4)) R_Quotient (
    .D({Dividend_p12[0], not_1_out}), .en(ld_quotient), .clk(Clk), .Q(Quotient), .clr(Reset));
  Register #(.width(5)) R_Rem (
    .D({Register_A_q[4], Dividend_p12[4:1]}), .en(ld_rem), .clk(Clk), .Q(Remainder), .clr(Reset));
endmodule

module five_bit_add_sub (
  input  Sub,
  input  [4:0] X,
  input  [4:0] Y,
  output [4:0] sum
);

  wire fa_2_c_o, fa_3_c_o, fa_4_c_o, fa_5_c_o, xor_1_out, xor_2_out, xor_3_out, xor_4_out, xor_5_out;

  xor xor_1 (xor_1_out, Sub, Y[4]);
  xor xor_2 (xor_2_out, Sub, Y[3]);
  xor xor_3 (xor_3_out, Sub, Y[2]);
  xor xor_4 (xor_4_out, Sub, Y[1]);
  xor xor_5 (xor_5_out, Sub, Y[0]);
  FA fa_1 (.c_i(fa_2_c_o), .a(X[4]), .b(xor_1_out), .s(sum[4]));  // open: c_o
  FA fa_2 (.c_i(fa_3_c_o), .a(X[3]), .b(xor_2_out), .s(sum[3]), .c_o(fa_2_c_o));
  FA fa_3 (.c_i(fa_4_c_o), .a(X[2]), .b(xor_3_out), .s(sum[2]), .c_o(fa_3_c_o));
  FA fa_4 (.c_i(fa_5_c_o), .a(X[1]), .b(xor_4_out), .s(sum[1]), .c_o(fa_4_c_o));
  FA fa_5 (.c_i(Sub), .a(X[0]), .b(xor_5_out), .s(sum[0]), .c_o(fa_5_c_o));
endmodule

module FA (
  input  c_i,
  input  a,
  input  b,
  output s,
  output c_o
);

  wire xor_1_out;

  xor xor_1 (xor_1_out, a, b);
  Multiplexer #(.enable("false")) multiplexer_1 (.in0(b), .in1(c_i), .out(c_o), .sel(xor_1_out));
  xor xor_2 (s, c_i, xor_1_out);
endmodule

module state_table (
  input  [4:0] state,
  input  MSB,
  output ld_Div_out,
  output ld_divisor,
  output ld_Div,
  output shift_Div,
  output Sub,
  output ld_sum,
  output ld_RegA,
  output ld_MSB,
  output ld_quotient,
  output ld_rem,
  output [4:0] next_st
);

  Ld_Div_out_state_table ld_div_out_state_table_1 (.state(state), .ld_Div_out(ld_Div_out));
  ld_divisor_state_table ld_divisor_state_table_1 (.state(state), .ld_divisor(ld_divisor));
  ld_Div_state_table ld_div_state_table_1 (.state(state), .ld_Div(ld_Div));
  shift_Div_state_table shift_div_state_table_1 (.state(state), .shift_Div(shift_Div));
  Sub_state_table sub_state_table_1 (.state(state), .Sub(Sub));
  ld_sum_state_table ld_sum_state_table_1 (.state(state), .ld_sum(ld_sum));
  ld_RegA_state_table ld_rega_state_table_1 (.state(state), .ld_RegA(ld_RegA));
  ld_MSB_state_table ld_msb_state_table_1 (.state(state), .ld_MSB(ld_MSB));
  ld_quotient_state_table ld_quotient_state_table_1 (.state(state), .ld_quotient(ld_quotient));
  ld_rem_state_table ld_rem_state_table_1 (.state(state), .ld_rem(ld_rem));
  next_state next_state_1 (.MSB(MSB), .state(state), .next_st(next_st));
endmodule

module next_state (
  input  MSB,
  input  [4:0] state,
  output [4:0] next_st
);

  wire and_1_out, and_2_out, and_3_out, and_4_out, and_5_out, and_6_out, and_7_out, and_8_out, and_9_out,
       and_10_out, and_11_out, and_12_out, and_13_out, and_14_out, and_15_out, and_16_out, and_17_out,
       and_18_out, and_19_out, and_20_out, and_21_out, and_22_out, and_23_out, and_24_out, not_1_out,
       not_2_out, not_3_out, not_4_out, not_5_out, not_6_out, not_7_out, not_8_out, not_9_out, not_10_out,
       not_11_out, not_12_out, not_13_out, not_14_out, not_15_out, not_16_out, not_17_out, not_18_out,
       not_19_out, not_20_out, not_21_out, not_22_out, not_23_out;

  not not_1 (not_1_out, state[2]);
  not not_2 (not_2_out, state[0]);
  not not_3 (not_3_out, state[3]);
  not not_4 (not_4_out, MSB);
  not not_5 (not_5_out, state[4]);
  not not_6 (not_6_out, state[1]);
  not not_7 (not_7_out, state[2]);
  not not_8 (not_8_out, state[1]);
  not not_9 (not_9_out, state[0]);
  not not_10 (not_10_out, state[0]);
  not not_11 (not_11_out, state[2]);
  not not_12 (not_12_out, state[0]);
  not not_13 (not_13_out, MSB);
  not not_14 (not_14_out, state[3]);
  not not_15 (not_15_out, MSB);
  not not_16 (not_16_out, state[4]);
  not not_17 (not_17_out, state[1]);
  not not_18 (not_18_out, state[2]);
  not not_19 (not_19_out, state[3]);
  not not_20 (not_20_out, state[2]);
  not not_21 (not_21_out, state[1]);
  not not_22 (not_22_out, state[0]);
  not not_23 (not_23_out, state[3]);
  and and_1 (and_1_out, not_1_out, not_2_out);
  and and_2 (and_2_out, not_2_out, MSB);
  and and_3 (and_3_out, state[4], not_2_out);
  and and_4 (and_4_out, not_3_out, state[1], not_2_out);
  and and_5 (and_5_out, state[3], not_8_out, not_2_out);
  and and_6 (and_6_out, state[4], state[1], not_4_out);
  and and_7 (and_7_out, state[3], not_1_out, not_8_out, not_4_out);
  and and_8 (and_8_out, not_5_out, not_6_out, state[0]);
  and and_9 (and_9_out, not_7_out, not_6_out, state[0]);
  and and_10 (and_10_out, state[1], not_9_out, MSB);
  and and_11 (and_11_out, not_7_out, state[1], not_9_out);
  and and_12 (and_12_out, not_5_out, not_14_out, state[2], not_9_out, not_15_out);
  and and_13 (and_13_out, not_16_out, state[2], not_17_out);
  and and_14 (and_14_out, not_18_out, state[1], state[0]);
  and and_15 (and_15_out, not_19_out, state[2], not_10_out);
  and and_16 (and_16_out, state[2], not_10_out, MSB);
  and and_17 (and_17_out, state[3], not_20_out);
  and and_18 (and_18_out, state[3], not_21_out);
  and and_19 (and_19_out, state[3], not_22_out, MSB);
  and and_20 (and_20_out, not_23_out, state[2], state[1], state[0]);
  and and_21 (and_21_out, state[4], not_11_out);
  and and_22 (and_22_out, state[4], not_12_out);
  and and_23 (and_23_out, state[3], state[2], state[1], not_13_out);
  and and_24 (and_24_out, state[3], state[2], state[1], state[0]);
  or or_1 (next_st[0], and_1_out, and_2_out, and_3_out, and_4_out, and_5_out, and_6_out, and_7_out);
  or or_2 (next_st[1], and_8_out, and_9_out, and_10_out, and_11_out, and_12_out);
  or or_3 (next_st[2], and_13_out, and_14_out, and_15_out, and_16_out);
  or or_4 (next_st[3], and_17_out, and_18_out, and_19_out, and_20_out);
  or or_5 (next_st[4], and_21_out, and_22_out, and_23_out, and_24_out);
endmodule

module Ld_Div_out_state_table (
  input  [4:0] state,
  output ld_Div_out
);

  wire not_1_out, not_2_out, not_3_out, not_4_out;

  not not_1 (not_1_out, state[1]);
  not not_2 (not_2_out, state[2]);
  nand nand_1 (ld_Div_out, not_1_out, not_2_out, not_3_out, not_4_out);
  not not_3 (not_3_out, state[3]);
  not not_4 (not_4_out, state[4]);
endmodule

module ld_divisor_state_table (
  input  [4:0] state,
  output ld_divisor
);

  wire not_1_out, not_2_out, not_3_out, not_4_out;

  not not_1 (not_1_out, state[1]);
  not not_2 (not_2_out, state[2]);
  not not_3 (not_3_out, state[3]);
  not not_4 (not_4_out, state[4]);
  and and_1 (ld_divisor, state[0], not_1_out, not_2_out, not_3_out, not_4_out);
endmodule

module ld_Div_state_table (
  input  [4:0] state,
  output ld_Div
);

  wire and_1_out, and_2_out, and_3_out, and_4_out, not_1_out, not_2_out, not_3_out, not_4_out, not_5_out,
       not_6_out, not_7_out, not_8_out, not_9_out, not_10_out, not_11_out, not_12_out, not_13_out;

  not not_1 (not_1_out, state[1]);
  not not_2 (not_2_out, state[2]);
  not not_3 (not_3_out, state[3]);
  not not_4 (not_4_out, state[4]);
  not not_5 (not_5_out, state[0]);
  not not_6 (not_6_out, state[3]);
  not not_7 (not_7_out, state[4]);
  not not_8 (not_8_out, state[2]);
  not not_9 (not_9_out, state[4]);
  not not_10 (not_10_out, state[0]);
  not not_11 (not_11_out, state[1]);
  not not_12 (not_12_out, state[2]);
  not not_13 (not_13_out, state[3]);
  and and_1 (and_1_out, state[0], not_1_out, not_2_out, not_3_out, not_4_out);
  and and_2 (and_2_out, not_5_out, state[1], state[2], not_6_out, not_7_out);
  and and_3 (and_3_out, state[0], state[1], not_8_out, state[3], not_9_out);
  and and_4 (and_4_out, not_10_out, not_11_out, not_12_out, not_13_out, state[4]);
  or or_1 (ld_Div, and_1_out, and_2_out, and_3_out, and_4_out);
endmodule

module shift_Div_state_table (
  input  [4:0] state,
  output shift_Div
);

  wire and_1_out, and_2_out, and_3_out, and_4_out, not_1_out, not_2_out, not_3_out, not_4_out, not_5_out,
       not_6_out, not_7_out, not_8_out, not_9_out, not_10_out, not_11_out, not_12_out, not_13_out;
  wire [4:0] subtractor_1_out;

  Subtractor #(.width(5)) subtractor_1 (.a(state), .b(5'b00001), .out(subtractor_1_out));  // open: bin, bout
  not not_1 (not_1_out, subtractor_1_out[1]);
  not not_2 (not_2_out, subtractor_1_out[2]);
  not not_3 (not_3_out, subtractor_1_out[3]);
  not not_4 (not_4_out, subtractor_1_out[4]);
  not not_5 (not_5_out, subtractor_1_out[0]);
  not not_6 (not_6_out, subtractor_1_out[3]);
  not not_7 (not_7_out, subtractor_1_out[4]);
  not not_8 (not_8_out, subtractor_1_out[2]);
  not not_9 (not_9_out, subtractor_1_out[4]);
  not not_10 (not_10_out, subtractor_1_out[0]);
  not not_11 (not_11_out, subtractor_1_out[1]);
  not not_12 (not_12_out, subtractor_1_out[2]);
  not not_13 (not_13_out, subtractor_1_out[3]);
  and and_1 (and_1_out, subtractor_1_out[0], not_1_out, not_2_out, not_3_out, not_4_out);
  and and_2 (and_2_out, not_5_out, subtractor_1_out[1], subtractor_1_out[2], not_6_out, not_7_out);
  and and_3 (and_3_out, subtractor_1_out[0], subtractor_1_out[1], not_8_out, subtractor_1_out[3], not_9_out);
  and and_4 (and_4_out, not_10_out, not_11_out, not_12_out, not_13_out, subtractor_1_out[4]);
  or or_1 (shift_Div, and_1_out, and_2_out, and_3_out, and_4_out);
endmodule

module Sub_state_table (
  input  [4:0] state,
  output Sub
);

  wire and_1_out, and_2_out, and_3_out, and_4_out, not_1_out, not_2_out, not_3_out, not_4_out, not_5_out,
       not_6_out, not_7_out, not_8_out, not_9_out, not_10_out;

  not not_1 (not_1_out, state[1]);
  not not_2 (not_2_out, state[3]);
  not not_3 (not_3_out, state[4]);
  not not_4 (not_4_out, state[0]);
  not not_5 (not_5_out, state[2]);
  not not_6 (not_6_out, state[4]);
  not not_7 (not_7_out, state[4]);
  not not_8 (not_8_out, state[0]);
  not not_9 (not_9_out, state[1]);
  not not_10 (not_10_out, state[3]);
  and and_1 (and_1_out, state[0], not_1_out, state[2], not_2_out, not_3_out);
  and and_2 (and_2_out, not_4_out, state[1], not_5_out, state[3], not_6_out);
  and and_3 (and_3_out, state[0], state[1], state[2], state[3], not_7_out);
  and and_4 (and_4_out, not_8_out, not_9_out, state[2], not_10_out, state[4]);
  nor nor_1 (Sub, and_1_out, and_2_out, and_3_out, and_4_out);
endmodule

module ld_sum_state_table (
  input  [4:0] state,
  output ld_sum
);

  wire and_1_out, and_2_out, and_3_out, and_4_out, and_5_out, and_6_out, not_1_out, not_2_out, not_3_out,
       not_4_out, not_5_out, not_6_out;

  not not_1 (not_1_out, state[2]);
  not not_2 (not_2_out, state[0]);
  not not_3 (not_3_out, state[4]);
  and and_1 (and_1_out, state[3], not_1_out, not_2_out);
  and and_2 (and_2_out, state[3], state[2], state[0]);
  and and_3 (and_3_out, state[4], state[1], not_2_out);
  and and_4 (and_4_out, state[4], state[2], not_2_out);
  and and_5 (and_5_out, not_3_out, state[2], not_4_out, state[0]);
  not not_4 (not_4_out, state[1]);
  not not_5 (not_5_out, state[3]);
  not not_6 (not_6_out, state[2]);
  and and_6 (and_6_out, not_3_out, not_5_out, not_6_out, state[1], state[0]);
  or or_1 (ld_sum, and_1_out, and_2_out, and_3_out, and_4_out, and_5_out, and_6_out);
endmodule

module ld_RegA_state_table (
  input  [4:0] state,
  output ld_RegA
);

  wire and_1_out, and_2_out, and_3_out, and_4_out, and_5_out, and_6_out, not_1_out, not_2_out, not_3_out,
       not_4_out, not_5_out, not_6_out, not_7_out;

  not not_1 (not_1_out, state[4]);
  not not_2 (not_2_out, state[0]);
  not not_3 (not_3_out, state[3]);
  not not_4 (not_4_out, state[1]);
  not not_5 (not_5_out, state[2]);
  not not_6 (not_6_out, state[0]);
  not not_7 (not_7_out, state[2]);
  and and_1 (and_1_out, not_1_out, state[2], state[0]);
  and and_2 (and_2_out, not_5_out, state[1], not_6_out);
  and and_3 (and_3_out, state[4], state[2], not_2_out);
  and and_4 (and_4_out, not_1_out, not_3_out, not_5_out, state[1]);
  and and_5 (and_5_out, state[3], not_4_out, not_2_out);
  and and_6 (and_6_out, state[4], not_7_out, not_4_out, state[0]);
  or or_1 (ld_RegA, and_1_out, and_2_out, and_3_out, and_4_out, and_5_out, and_6_out);
endmodule

module ld_MSB_state_table (
  input  [4:0] state,
  output ld_MSB
);

  wire and_1_out, and_2_out, and_3_out, and_4_out, not_1_out, not_2_out, not_3_out, not_4_out, not_5_out,
       not_6_out, not_7_out, not_8_out, not_9_out, not_10_out, not_11_out, not_12_out, not_13_out;
  wire [4:0] subtractor_1_out;

  Subtractor #(.width(5)) subtractor_1 (.a(state), .b(5'b00010), .out(subtractor_1_out));  // open: bin, bout
  not not_1 (not_1_out, subtractor_1_out[1]);
  not not_2 (not_2_out, subtractor_1_out[2]);
  not not_3 (not_3_out, subtractor_1_out[3]);
  not not_4 (not_4_out, subtractor_1_out[4]);
  not not_5 (not_5_out, subtractor_1_out[0]);
  not not_6 (not_6_out, subtractor_1_out[3]);
  not not_7 (not_7_out, subtractor_1_out[4]);
  not not_8 (not_8_out, subtractor_1_out[2]);
  not not_9 (not_9_out, subtractor_1_out[4]);
  not not_10 (not_10_out, subtractor_1_out[0]);
  not not_11 (not_11_out, subtractor_1_out[1]);
  not not_12 (not_12_out, subtractor_1_out[2]);
  not not_13 (not_13_out, subtractor_1_out[3]);
  and and_1 (and_1_out, subtractor_1_out[0], not_1_out, not_2_out, not_3_out, not_4_out);
  and and_2 (and_2_out, not_5_out, subtractor_1_out[1], subtractor_1_out[2], not_6_out, not_7_out);
  and and_3 (and_3_out, subtractor_1_out[0], subtractor_1_out[1], not_8_out, subtractor_1_out[3], not_9_out);
  and and_4 (and_4_out, not_10_out, not_11_out, not_12_out, not_13_out, subtractor_1_out[4]);
  or or_1 (ld_MSB, and_1_out, and_2_out, and_3_out, and_4_out);
endmodule

module ld_quotient_state_table (
  input  [4:0] state,
  output ld_quotient
);

  wire not_1_out, not_2_out;

  not not_1 (not_1_out, state[1]);
  and and_1 (ld_quotient, state[0], not_1_out, state[2], not_2_out, state[4]);
  not not_2 (not_2_out, state[3]);
endmodule

module ld_rem_state_table (
  input  [4:0] state,
  output ld_rem
);

  wire not_1_out, not_2_out;

  not not_1 (not_1_out, state[1]);
  and and_1 (ld_rem, state[0], not_1_out, state[2], not_2_out, state[4]);
  not not_2 (not_2_out, state[3]);
endmodule

module FSM (
  input  [3:0] Dividend,
  input  [3:0] Divisor,
  input  Enable,
  input  Reset,
  output [3:0] Quotient,
  output [4:0] Remainder,
  output [4:0] out_7
);

  wire clock_1_out, datapath_1_msb, state_table_1_ld_div, state_table_1_ld_div_out, state_table_1_ld_divisor,
       state_table_1_ld_msb, state_table_1_ld_quotient, state_table_1_ld_rega, state_table_1_ld_rem,
       state_table_1_ld_sum, state_table_1_shift_div, state_table_1_sub;
  wire [3:0] bit_extender_1_out;
  wire [4:0] state_table_1_next_st;

  state_table state_table_1 (
    .state(out_7), .MSB(datapath_1_msb), .ld_Div_out(state_table_1_ld_div_out),
    .ld_divisor(state_table_1_ld_divisor), .ld_Div(state_table_1_ld_div),
    .shift_Div(state_table_1_shift_div), .Sub(state_table_1_sub), .ld_sum(state_table_1_ld_sum),
    .ld_RegA(state_table_1_ld_rega), .ld_MSB(state_table_1_ld_msb), .ld_quotient(state_table_1_ld_quotient),
    .ld_rem(state_table_1_ld_rem), .next_st(state_table_1_next_st));
  Clock clock_1 (.out(clock_1_out));
  Register #(.width(5)) register_1 (.D(state_table_1_next_st), .en(Enable), .clk(clock_1_out), .Q(out_7), .clr(Reset));
  Hex_Digit_Display hex_digit_display_1 (.value(Dividend));  // open: dp
  Hex_Digit_Display hex_digit_display_2 (.value(Divisor));  // open: dp
  datapath datapath_1 (
    .Dividend_Val(Dividend), .ld_Div_out(state_table_1_ld_div_out), .Divisor_Val(Divisor),
    .ld_divisor(state_table_1_ld_divisor), .Clk(clock_1_out), .ld_Div(state_table_1_ld_div),
    .shift_Div(state_table_1_shift_div), .Sub(state_table_1_sub), .ld_quotient(state_table_1_ld_quotient),
    .ld_MSB(state_table_1_ld_msb), .ld_sum(state_table_1_ld_sum), .ld_rem(state_table_1_ld_rem),
    .ld_RegA(state_table_1_ld_rega), .Reset(Reset), .Quotient(Quotient), .MSB(datapath_1_msb),
    .Remainder(Remainder));
  Hex_Digit_Display hex_digit_display_3 (.value(Quotient));  // open: dp
  Hex_Digit_Display hex_digit_display_4 (.value(bit_extender_1_out));  // open: dp
  Bit_Extender #(.in_width(5), .out_width(4)) bit_extender_1 (.in(Remainder), .out(bit_extender_1_out));

  // Notes on the sheet:
  //   ÷
  //   Quotient
  //   Remainder
endmodule

module D_Latch (
  input  D,
  input  Clk,
  output Qa,
  output Qb
);

  wire nand_1_out, nand_2_out, not_1_out;

  not not_1 (not_1_out, D);
  nand nand_1 (nand_1_out, D, Clk);
  nand nand_2 (nand_2_out, Clk, not_1_out);
  nand nand_3 (Qa, nand_1_out, Qb);
  nand nand_4 (Qb, Qa, nand_2_out);
endmodule
